# Fritzing sketch LDR (saved by Fritzing 0.9.3b)
circuit board: 8.46667cm x 5.64444cm
breadboards: 1

parts:
  R1 = Resistor [tolerance=±5% resistance=220 package="0603 [SMD]"]
  R2 = Photocell (LDR) [package=THT]
  LED1 = LED - 3mm [color="Red (633nm)" package="3 mm [THT]"]
  Componente1 = Arduino Uno (Rev3) - ICSP
  R3 = Resistor [tolerance=±5% resistance=220 package="0603 [SMD]"]

nets:
  N1: R1.Pin_0, Componente1.GND, R3.Pin_0
  N2: R1.Pin_1, LED1.cathode
  N3: R2.pin_0, Componente1.5V
  N4: R2.pin_1, Componente1.A0, R3.Pin_1
  N5: LED1.anode, Componente1.D6_PWM

// code stored in the sketch: LDR.ino
#define LED 6
int LDR;

void setup(){
	Serial.begin(115200);
	pinMode(LED, OUTPUT);
}

void loop(){
	LDR = analogRead(A0);
	if(LDR < 400){
		digitalWrite(LED, HIGH);
	}else{
		digitalWrite(LED, LOW);
	}
	Serial.println(LDR);
}
