# Fritzing sketch exercicio1 (saved by Fritzing 0.9.3b)
breadboards: 1

parts:
  Componente1 = Arduino Uno (Rev3)
  R2 = Photocell (LDR) [package=THT]
  R3 = Temperature Sensor (Thermistor) [thermistor_type=NTC package=THT]
  R4 = Resistor [tolerance=±5% resistance=10k package="0805 [SMD]"]
  LED1 = smd LED [color="Red (633nm)" package="1206 [SMD]"]
  J1 = Basic Servo
  R5 = Resistor [tolerance=±5% resistance=220 package="0805 [SMD]"]
  R1 = Resistor [tolerance=±5% resistance=10k package=THT]
  C1 = Capacitor Polarized [package=cpol-radial-10uf-25v]

nets:
  N1: Componente1.A4/SDA, R2.pin_1, R1.Pin_0
  N2: Componente1.A5/SCL, R3.pin_1, R4.Pin_0
  N3: Componente1.D11_PWM/MOSI, J1.pulse
  N4: Componente1.D4, LED1.cathode
  N5: Componente1.5V, R2.pin_0, R3.pin_0, C1.+
  GND: Componente1.GND, R4.Pin_1, J1.gnd, R5.Pin_0, R1.Pin_1, C1.-
  N6: LED1.anode, R5.Pin_1

// code stored in the sketch: servomotor.ino
#include <Servo.h>
 
#define SERVO 11    // Porta Digital 11 PWM
#define LED 4       //Porta do LED

Servo s;            // Variável Servo
int pos;            // Posiçao Servo
int luminosidade;   // Variável para armazenar valor de luminosidade
float temperatura;  // Variável para armazenar valor de temperatura

 
void setup ()
{
  s.attach(SERVO);
  Serial.begin(115200);
  s.write(0); // Inicia motor posiçao zero
  pinMode(LED, OUTPUT);
}
 
void loop(){
  ligaLuz();
  ligaVentilador();
}

void ligaVentilador{
  temperatura = analogRead(A5)*0.0048;
  if(temeratura > 25){
    for(pos = 0; pos <= 180; pos++){
      s.write(pos);
      delay(15);
    }
    delay(1000);
    for(pos = 180; pos >= 0; pos--){
      s.write(pos);
      delay(5);
    }
    delay(1000);
  }
}

void LigaLuz(){
   luminosidade = analogRead(A4);
   if(luminosidade  < 400){
    digitalWrite(LED, HIGH);
  }else{
    digitalWrite(LED, LOW);
  }
    
}
