# Fritzing sketch LEDs1 (saved by Fritzing 0.9.3b)
circuit board: 8.46667cm x 5.64444cm
breadboards: 1

parts:
  Part1 = Arduino Uno (Rev3)
  R3 = Resistor [tolerance=±5% resistance=220 package=THT]
  LED2 = LED - 5mm [color="Red (633nm)" package="5 mm [THT]"]

nets:
  N1: Part1.GND, R3.Pin_0
  N2: Part1.D6_PWM, LED2.anode
  N3: R3.Pin_1, LED2.cathode

notes:
  Primeiro exercicio com LEDs e Arduinno

// code stored in the sketch: LEDs1.ino
#define LED 6

void setup() {
  // put your setup code here, to run once:
	pinMode(LED, OUTPUT);

}

void loop() {
  // put your main code here, to run repeatedly:

	digitalWrite(LED, HIGH);
	delay(1000);
	digitalWrite(LED, LOW);
	delay(1000);
}

// code stored in the sketch: MIFARE_hakcing.ino

