# Fritzing sketch servomotor (saved by Fritzing 0.9.3b)
breadboards: 1

parts:
  Componente1 = Arduino Uno (Rev3)
  J1 = Basic Servo
  C1 = Capacitor Polarized [package=cpol-radial-10uf-25v]

nets:
  N1: Componente1.D11_PWM/MOSI, J1.pulse
  N2: Componente1.5V, C1.+
  GND: Componente1.GND, J1.gnd, C1.-

// code stored in the sketch: servomotor.ino
#include <Servo.h>
 
#define SERVO 11    // Porta Digital 11 PWM

Servo s;            // Variavel Servo
int pos;            // Posiçao Servo
 
void setup ()
{
  s.attach(SERVO);
  Serial.begin(115200);
  s.write(0); // Inicia motor posiçao zero
}
 
void loop(){
	if(Serial.available()){
    for(pos = 0; pos <= 180; pos++){
      s.write(pos);
      delay(15);
    }
    delay(1000);
    for(pos = 180; pos >= 0; pos--){
      s.write(pos);
      delay(5);
    }
    delay(1000);
  }
}
