# Fritzing sketch ultrasonic (saved by Fritzing 0.9.3b)
circuit board: 8.46667cm x 5.64444cm
breadboards: 1

parts:
  hc-sr1 = hc-sr04
  Componente1 = Arduino Uno (Rev3)
  C1 = Electrolytic Capacitor [capacitance=1µF package="100 mil [THT, electrolytic]"]

nets:
  VCC: hc-sr1.VCC, Componente1.5V, C1.+
  N1: hc-sr1.Trig, Componente1.D5_PWM
  N2: hc-sr1.Echo, Componente1.D4
  GND: hc-sr1.GND, Componente1.GND, C1.-

// code stored in the sketch: ultrasonic.ino
//Define os pinos para o trigger e echo
#define pino_trigger 5
#define pino_echo 4
 
//Inicializa o sensor nos pinos definidos acima
 
void setup()
{
  pinMode(pino_trigger, OUTPUT);
  pinMode(pino_echo, INPUT);
  Serial.begin(9600);
  Serial.println("Lendo dados do sensor...");
}
 
void loop(){
  digitalWrite(pino_trigger, LOW);
  delayMicroseconds(2);
  digitalWrite(pino_trigger, HIGH);
  delayMicroseconds(10);
  digitalWrite(pino_trigger, LOW);
  long usec = pulseIn(pino_echo , HIGH);
  Serial.print("distancia em cm: ");
  Serial.println(usec*0.000001*34000/2);
  delay(1000);
}
