# Fritzing sketch semaforo (saved by Fritzing 0.9.3b)
circuit board: 7.55361cm x 6.96768cm
breadboards: 1

parts:
  Part1 = Arduino Uno (Rev3)
  R1 = Resistor [tolerance=±5% resistance=220 package=THT]
  LED1 = LED - 5mm [color="Red (633nm)" package="5 mm [THT]"]
  LED2 = LED - 5mm [color="Yellow (595nm)" package="5 mm [THT]"]
  LED3 = LED - 5mm [color="Green (555nm)" package="5 mm [THT]"]
  LED4 = LED - 5mm [color="Red (633nm)" package="5 mm [THT]"]
  LED5 = LED - 5mm [color="Green (555nm)" package="5 mm [THT]"]
  S1 = Pushbutton [package="[THT]"]
  R2 = Resistor [tolerance=±5% resistance=220 package=THT]
  R3 = Resistor [tolerance=±5% resistance=220 package=THT]
  R5 = Resistor [tolerance=±5% resistance=220 package=THT]
  R4 = Resistor [tolerance=±5% resistance=220 package=THT]
  R6 = Resistor [tolerance=±5% resistance=220 package=THT]

nets:
  N1: Part1.D9_PWM, S1.Pin_1, S1.Pin_2, R6.Pin_0
  N2: Part1.D10_PWM/SS, LED3.anode
  N3: Part1.D11_PWM/MOSI, LED2.anode
  N4: Part1.D12/MISO, LED1.anode
  N5: Part1.GND, R1.Pin_1, R2.Pin_1, R3.Pin_1, R5.Pin_1, R4.Pin_1, R6.Pin_1
  N6: Part1.D2, LED5.anode
  N7: Part1.D3_PWM, LED4.anode
  N8: Part1.5V, S1.Pin_3, S1.Pin_4
  N9: R1.Pin_0, LED1.cathode
  N10: LED2.cathode, R2.Pin_0
  N11: LED3.cathode, R3.Pin_0
  N12: LED4.cathode, R4.Pin_0
  N13: LED5.cathode, R5.Pin_0

// code stored in the sketch: semaforo.ino
#define ledCarroVermelho 		12
#define ledCarroAmarelo  		11
#define ledCarroVerde    		10
#define botao						 		9
#define ledPedestreVermelho 3
#define ledPedestreVerde	  2

void setup(){
	pinMode(ledCarroVermelho, OUTPUT);
	pinMode(ledCarroAmarelo, OUTPUT);
	pinMode(ledCarroVerde, OUTPUT);
	pinMode(ledPedestreVermelho, OUTPUT);
	pinMode(ledPedestreVerde, OUTPUT);
	pinMode(botao, INPUT);
}

void loop(){
	if(digitalRead(botao)){
		delay(300);
		digitalWrite(ledCarroVerde, LOW);
		digitalWrite(ledCarroAmarelo, HIGH);
		delay(1000);
		digitalWrite(ledCarroAmarelo, LOW);
		digitalWrite(ledCarroVermelho, HIGH);
		digitalWrite(ledPedestreVermelho, LOW);
		digitalWrite(ledPedestreVerde, HIGH);
		delay(5000);

	}else{
		digitalWrite(ledCarroVermelho, LOW);
		digitalWrite(ledCarroAmarelo, LOW);
		digitalWrite(ledCarroVerde, HIGH);
		digitalWrite(ledPedestreVermelho, HIGH);
		digitalWrite(ledPedestreVerde, LOW);
	}

}
